# Fritzing sketch Alice (saved by Fritzing 0.9.2b)
circuit board: 4.23304cm x 2.67379cm
breadboards: 1

parts:
  U1 = MIC [package=mic-9.7mm]
  R1 = Resistor [tolerance=±5% resistance=1G package=THT]
  R3 = Resistor [tolerance=±5% resistance=2.43k package=THT]
  R7 = Resistor [tolerance=±5% resistance=330 package=THT]
  R5 = Resistor [tolerance=±5% resistance=100k package=THT]
  D1 = Zener Diode [part_number=78-1N5242B breakdown_voltage=12.1V package="300 mil [THT]"]
  C3 = Electrolytic Capacitor [capacitance=0.1mF voltage=16V package="100 mil [THT, electrolytic]"]
  C2 = Ceramic Capacitor [capacitance=0.47mF package="200 mil [THT, multilayer]"]
  J1 = female pin header, 3 pins [form="♀ (female)" part_number=XLR]
  Q3 = PNP-Transistor [part_number=2N5087 package="TO92 [THT]"]
  C1 = Ceramic Capacitor [capacitance=0.47mF voltage=16V package="200 mil [THT, multilayer]"]
  R4 = Resistor [tolerance=±5% resistance=100k package=THT]
  Q2 = PNP-Transistor [part_number=2N5087 package="TO92 [THT]"]
  R2 = Resistor [tolerance=±5% resistance=2.43k package=THT]
  C4 = Electrolytic Capacitor [capacitance=10µF voltage=16V package="100 mil [THT, electrolytic]"]
  Q1 = MOSFET-NCHANNEL [package=to220v]
  R6 = Resistor [tolerance=±5% resistance=6.8k package=THT]

nets:
  GND: U1.1, R1.Pin_1, R3.Pin_1, D1.anode, C3.-, J1.pin1, C4.-
  N1: U1.2, R1.Pin_0, Q1.G
  N2: R3.Pin_0, C2.0, Q1.S
  N3: R7.Pin_0, C3.+, R2.Pin_0
  N4: R7.Pin_1, D1.cathode, C4.+, R6.Pin_1
  N5: R5.Pin_0, Q3.C, R4.Pin_1, Q2.C, R6.Pin_0
  N6: R5.Pin_1, C2.1, Q3.B
  N7: J1.pin2, Q3.E
  N8: J1.pin3, Q2.E
  N9: C1.0, R2.Pin_1, Q1.D
  N10: C1.1, R4.Pin_0, Q2.B
